# Fritzing sketch Doctor's Assistant (saved by Fritzing 0.9.3b)
breadboards: 1

parts:
  U1 = NodeMCU V1.0
  U2 = POT [package=pot_alpha_rv16af-20]
  hc-sr1 = hc-sr04
  LED1 = smd LED [color="Red (633nm)" package="0805 [SMD]"]
  LED2 = smd LED [color="Red (633nm)" package="1206 [SMD]"]
  R1 = Resistor [tolerance=±5% resistance=220 package=THT]
  R2 = Resistor [tolerance=±5% resistance=220 package=THT]

nets:
  N1: U1.D1, U1.TX, hc-sr1.Trig
  N2: U1.D2, hc-sr1.Echo
  VIN: U1.Vin, U2.A, hc-sr1.VCC
  GND: U1.GND, U2.E, hc-sr1.GND, LED1.cathode, LED2.cathode
  N3: U1.A0, U2.S
  N4: LED1.anode, R2.Pin_0
  N5: LED2.anode, R1.Pin_0

notes:
  Doctor's Assistant
  By CHOKCHAI

custom parts:
  NodeMCU V1.0: ESP8266 based NodeMCU V1.0
